# Fritzing sketch BME280 (saved by Fritzing 1.0.1rc)
breadboards: 1

parts:
  Onderdeel1 = Arduino Uno (Rev3) - ICSP
  Onderdeel2 = GY-BMEP280 Barometric Pressure Sensor - Breakout

nets:
  N1: Onderdeel1.D12/MISO, Onderdeel2.SDO
  GND: Onderdeel1.GND, Onderdeel2.GND

notes:
  Vcc 3V3 GND SCK SDI CSB SDO <-SPI
  SCL SDA <-IIC

custom parts:
  GY-BMEP280 Barometric Pressure Sensor - Breakout: The BME280 is a chip which was originally designed for the next generation of smartphones. It is made up of a very accurate pressure sensor and an associated temperature sensor which helps calibrate the pressure readings. And just for fun they threw in a pretty solid humidity sensor in there as well! So with an I2C connection you have access to enough weather data to make some pretty good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
