# Fritzing sketch PWM (saved by Fritzing 0.9.10b)
breadboards: 1

parts:
  F1 = Fan - Ventilador [package=THT]
  Onderdeel2 = Arduino Uno (Rev3)

nets:
  GND: F1.GND, Onderdeel2.GND

notes:
  12V

custom parts:
  Fan - Ventilador: Ventilador de 2 pines, se encuentra comunmente en computadoras de escritorio
